# Fritzing sketch shema-electronique (saved by Fritzing 0.9.6b)

parts:
  raspberry_pi_4 = Raspberry Pi 4 [part_number=RPI-4-b]
  J1 = Basic Servo
  M2 = ESC
  920KV_Motor2 = DJI 920 KV Motor
  S1 = Pushbutton [package="[THT]"]
  R1 = Resistor [tolerance=±5% resistance=23 package="0603 [SMD]"]
  LED1 = smd LED [color="Red (633nm)" package="0603 [SMD]"]
  Resistor = Resistor [tolerance=±5% resistance=330 package="2010 [SMD]"]
  Power_plug3 = Power plug  # not connected
  Mod1 = KY-022 Infrared Receiver Module [package="Breakout board"]

nets (from the breadboard view):
  3V3: raspberry_pi_4.3v3, raspberry_pi_4.GPIO2, raspberry_pi_4.3V3, raspberry_pi_4.GPIO10, S1.Pin_2, Mod1.Vin
  N1: raspberry_pi_4.GPIO17, raspberry_pi_4.GPIO27, Mod1.S
  N2: raspberry_pi_4.GPIO13, M2.DATA
  GND: raspberry_pi_4.GND, raspberry_pi_4.GPIO24, J1.gnd, M2.GND, R1.Pin_0, Resistor.Pin_0, Mod1.-
  N3: raspberry_pi_4.GPIO12, J1.pulse
  N4: raspberry_pi_4.GPIO15, raspberry_pi_4.GPIO14, LED1.anode
  VCC: J1.vcc, M2.5V
  N5: M2.U, 920KV_Motor2.u
  N6: M2.V, 920KV_Motor2.v
  N7: M2.W, 920KV_Motor2.w
  N8: S1.Pin_3, S1.Pin_4, R1.Pin_1

notes:
  INPUT 7,2V
  ECS 25A
  BRUSHLESS MOTOR
  SERVO FOR CAR DIRECTION
  RASPBERRY 4
  SHUTDOWN BUTTON
  LED INDICATOR
  INFRARED SENSOR

custom parts:
  Raspberry Pi 4: The RPi4, a faster version of the awesome Raspberry Pi 2 B ARM Board with 40 pin gpio. Ready for special Raspberry Pi B+ and RPi2 Hat (Hardware attached (on) top)
  DJI 920 KV Motor: DJI Brushless Outrunner 2212/920K Motor F330-550
  KY-022 Infrared Receiver Module: KY-022 IR receiver module, reacts to 38kHz infrared light.

// code stored in the sketch: Untitled.ino

